// Logisim project logic.circ as structural Verilog: 8 circuits, main circuit main
module main (
  input  INPUT_LOAD,
  input  OUTPUT,
  input  IDU_INCREMENT,
  input  IDU_DECREMENT,
  input  REG_A_SET,
  input  REG_A_LOAD_IDU,
  input  REG_A_LOAD_BUS,
  input  REG_MC_SET_LOW,
  input  REG_MC_SET_HIGH,
  input  REG_MC_LOAD_LOW,
  input  REG_MC_LOAD_HIGH,
  input  REG_MC_LOAD_16,
  input  REG_PC_SET_LOW,
  input  REG_PC_SET_HIGH,
  input  REG_PC_LOAD_LOW,
  input  REG_PC_LOAD_HIGH,
  input  REG_PC_SELECT_ROM,
  input  RAM_LOAD,
  input  RAM_STORE,
  output INPUT_READY,
  output IDU_OVERFLOW,
  output [7:0] INSTRUCTION,
  output ZERO_DETECT
);

  wire register_1_out0_0, register_1_out0_1, register_1_out0_2, register_1_out0_3, register_1_out0_4,
       register_1_out0_5, register_1_out0_6, register_1_out0_7;
  wire [6:0] bit_extender_1_out;
  wire [7:0] incrementationdecrementationunit_1_o0, register_1_out1_0;
  wire [15:0] n16bit_register_1__16out, n16bit_register_2__16out;

  Bit_Extender #(.out_width(7)) bit_extender_1 (.in(register_1_out1_0), .out(bit_extender_1_out));
  Register register_1 (
    .IN0_0(register_1_out1_0[0]), .IN0_1(register_1_out1_0[1]), .IN0_2(register_1_out1_0[2]),
    .IN0_3(register_1_out1_0[3]), .IN0_4(register_1_out1_0[4]), .IN0_5(register_1_out1_0[5]),
    .IN0_6(register_1_out1_0[6]), .IN0_7(register_1_out1_0[7]), .SET(REG_A_SET), .LOAD0(REG_A_LOAD_IDU),
    .LOAD1(REG_A_LOAD_BUS), .OUT0_0(register_1_out0_0), .OUT0_1(register_1_out0_1),
    .OUT0_2(register_1_out0_2), .OUT0_3(register_1_out0_3), .OUT0_4(register_1_out0_4),
    .OUT0_5(register_1_out0_5), .OUT0_6(register_1_out0_6), .OUT0_7(register_1_out0_7),
    .OUT1_0(register_1_out1_0[0]), .OUT1_1(register_1_out1_0[1]), .OUT1_2(register_1_out1_0[2]),
    .OUT1_3(register_1_out1_0[3]), .OUT1_4(register_1_out1_0[4]), .OUT1_5(register_1_out1_0[5]),
    .OUT1_6(register_1_out1_0[6]), .OUT1_7(register_1_out1_0[7]));
  assign register_1_out1_0 = INPUT_LOAD ? {8{1'b0}} : 8'bz;  // Controlled_Buffer controlled_buffer_1
  TTY #(.cols(60)) tty_1 (.data(bit_extender_1_out), .clk(OUTPUT));  // open: we, clr
  Pull_Resistor pull_resistor_1 (.node(register_1_out0_0));
  _16bit_Register u_16bit_register_1 (
    .SET_L(REG_MC_SET_LOW), .SET_H(REG_MC_SET_HIGH), .IN_L(register_1_out1_0), .LOAD_L(REG_MC_LOAD_LOW),
    .LOAD_16(REG_MC_LOAD_16), .LOAD_H(REG_MC_LOAD_HIGH), .IN_H(register_1_out1_0), .OUT_L(register_1_out1_0),
    .OUT_H(register_1_out1_0), ._16OUT(n16bit_register_1__16out));
  _16bit_Register u_16bit_register_2 (
    .SET_L(REG_PC_SET_LOW), .SET_H(REG_PC_SET_HIGH), .IN_L(register_1_out1_0), .LOAD_L(REG_PC_LOAD_LOW),
    .LOAD_16(REG_PC_SELECT_ROM), .LOAD_H(REG_PC_LOAD_HIGH), .IN_H(register_1_out1_0),
    .OUT_L(register_1_out1_0), .OUT_H(register_1_out1_0), ._16OUT(n16bit_register_2__16out));
  Zero_detect zero_detect_1 (
    .BUS0(register_1_out1_0[0]), .BUS1(register_1_out1_0[1]), .BUS2(register_1_out1_0[2]),
    .BUS3(register_1_out1_0[3]), .BUS4(register_1_out1_0[4]), .BUS5(register_1_out1_0[5]),
    .BUS6(register_1_out1_0[6]), .BUS7(register_1_out1_0[7]), .ZERO(ZERO_DETECT));
  Button button_1 (.out(INPUT_READY));
  assign register_1_out1_0 = REG_A_LOAD_IDU ? incrementationdecrementationunit_1_o0 : 8'bz;  // Controlled_Buffer controlled_buffer_2
  Pull_Resistor pull_resistor_2 (.node(register_1_out0_3));
  Pull_Resistor pull_resistor_3 (.node(register_1_out0_4));
  Pull_Resistor pull_resistor_4 (.node(register_1_out0_2));
  Pull_Resistor pull_resistor_5 (.node(register_1_out0_1));
  Pull_Resistor pull_resistor_6 (.node(register_1_out0_7));
  Pull_Resistor pull_resistor_7 (.node(register_1_out0_5));
  Pull_Resistor pull_resistor_8 (.node(register_1_out0_6));
  ROM #(.addrWidth(16)) rom_1 (.addr(n16bit_register_2__16out), .data(INSTRUCTION), .sel(REG_PC_SELECT_ROM));
  RAM #(.addrWidth(16)) ram_1 (
    .addr(n16bit_register_1__16out), .data(register_1_out1_0), .sel(1'b1), .clk(RAM_STORE), .ld(RAM_LOAD));  // open: clr
  IncrementationDecrementationUnit incrementationdecrementationunit_1 (
    .INCREMENT(IDU_INCREMENT), .DECREMENT(IDU_DECREMENT), .IN0(register_1_out0_0), .IN1(register_1_out0_1),
    .IN2(register_1_out0_2), .IN3(register_1_out0_3), .IN4(register_1_out0_4), .IN5(register_1_out0_5),
    .IN6(register_1_out0_6), .IN7(register_1_out0_7), .O0(incrementationdecrementationunit_1_o0[0]),
    .O1(incrementationdecrementationunit_1_o0[1]), .O2(incrementationdecrementationunit_1_o0[2]),
    .O3(incrementationdecrementationunit_1_o0[3]), .O4(incrementationdecrementationunit_1_o0[4]),
    .O5(incrementationdecrementationunit_1_o0[5]), .O6(incrementationdecrementationunit_1_o0[6]),
    .O7(incrementationdecrementationunit_1_o0[7]), .Overflow(IDU_OVERFLOW));

  // Notes on the sheet:
  //   ADDRESS BUS
  //   DATA BUS
  //   REG A
  //   input
  //   REG MC
  //   REG PC
  //   input_rdy
  //   PROGRAM ROM
  //   RAM
endmodule

module Full_Adder (
  input  A,
  input  B,
  input  Cin,
  output S,
  output Cout
);

  wire and_1_out, and_2_out, xor_1_out;

  xor xor_1 (xor_1_out, A, B);
  xor xor_2 (S, xor_1_out, Cin);
  and and_1 (and_1_out, xor_1_out, Cin);
  and and_2 (and_2_out, A, B);
  or or_1 (Cout, and_1_out, and_2_out);
endmodule

module _8_bit_Adder (
  input  A0,
  input  B0,
  input  A1,
  input  B1,
  input  A2,
  input  B2,
  input  A3,
  input  B3,
  input  A4,
  input  B4,
  input  A5,
  input  B5,
  input  A6,
  input  B6,
  input  A7,
  input  B7,
  output out_17,
  output out_18,
  output out_19,
  output out_20,
  output out_21,
  output out_22,
  output out_23,
  output out_24,
  output Overflow
);

  wire full_adder_1_cout, full_adder_2_cout, full_adder_3_cout, full_adder_4_cout, full_adder_5_cout,
       full_adder_6_cout, full_adder_7_cout;

  Full_Adder full_adder_1 (.A(A0), .B(B0), .Cin(1'b0), .S(out_17), .Cout(full_adder_1_cout));
  Full_Adder full_adder_2 (.A(A1), .B(B1), .Cin(full_adder_1_cout), .S(out_18), .Cout(full_adder_2_cout));
  Full_Adder full_adder_3 (.A(A2), .B(B2), .Cin(full_adder_2_cout), .S(out_19), .Cout(full_adder_3_cout));
  Full_Adder full_adder_4 (.A(A3), .B(B3), .Cin(full_adder_3_cout), .S(out_20), .Cout(full_adder_4_cout));
  Full_Adder full_adder_5 (.A(A4), .B(B4), .Cin(full_adder_4_cout), .S(out_21), .Cout(full_adder_5_cout));
  Full_Adder full_adder_6 (.A(A5), .B(B5), .Cin(full_adder_5_cout), .S(out_22), .Cout(full_adder_6_cout));
  Full_Adder full_adder_7 (.A(A6), .B(B6), .Cin(full_adder_6_cout), .S(out_23), .Cout(full_adder_7_cout));
  Full_Adder full_adder_8 (.A(A7), .B(B7), .Cin(full_adder_7_cout), .S(out_24), .Cout(Overflow));
endmodule

module IncrementationDecrementationUnit (
  input  INCREMENT,
  input  DECREMENT,
  input  IN0,
  input  IN1,
  input  IN2,
  input  IN3,
  input  IN4,
  input  IN5,
  input  IN6,
  input  IN7,
  output O0,
  output O1,
  output O2,
  output O3,
  output O4,
  output O5,
  output O6,
  output O7,
  output Overflow
);

  wire and_1_out, and_2_out, or_1_out;

  and and_1 (and_1_out, INCREMENT, 1'b1);
  and and_2 (and_2_out, DECREMENT, 1'b1);
  or or_1 (or_1_out, and_1_out, and_2_out);
  _8_bit_Adder u_8_bit_adder_1 (
    .A0(IN0), .B0(or_1_out), .A1(IN1), .B1(and_2_out), .A2(IN2), .B2(and_2_out), .A3(IN3), .B3(and_2_out),
    .A4(IN4), .B4(and_2_out), .A5(IN5), .B5(and_2_out), .A6(IN6), .B6(and_2_out), .A7(IN7), .B7(and_2_out),
    .out_17(O0), .out_18(O1), .out_19(O2), .out_20(O3), .out_21(O4), .out_22(O5), .out_23(O6), .out_24(O7),
    .Overflow(Overflow));
endmodule

module D_FF (
  input  Clock,
  input  D0,
  input  D1,
  input  D2,
  input  D3,
  input  D4,
  input  D5,
  input  D6,
  input  D7,
  output out_10,
  output out_11,
  output out_12,
  output out_13,
  output out_14,
  output out_15,
  output out_16,
  output out_17
);

  D_Flip_Flop d_ff_1 (.clk(Clock), .D(D0), .Q(out_10));  // open: Qn, preset, en, reset
  D_Flip_Flop d_ff_2 (.clk(Clock), .D(D1), .Q(out_11));  // open: Qn, preset, en, reset
  D_Flip_Flop d_ff_3 (.clk(Clock), .D(D2), .Q(out_12));  // open: Qn, preset, en, reset
  D_Flip_Flop d_ff_4 (.clk(Clock), .D(D3), .Q(out_13));  // open: Qn, preset, en, reset
  D_Flip_Flop d_ff_5 (.clk(Clock), .D(D4), .Q(out_14));  // open: Qn, preset, en, reset
  D_Flip_Flop d_ff_6 (.clk(Clock), .D(D5), .Q(out_15));  // open: Qn, preset, en, reset
  D_Flip_Flop d_ff_7 (.clk(Clock), .D(D6), .Q(out_16));  // open: Qn, preset, en, reset
  D_Flip_Flop d_ff_8 (.clk(Clock), .D(D7), .Q(out_17));  // open: Qn, preset, en, reset
endmodule

module Register (
  input  SET,
  input  IN0_0,
  input  IN0_1,
  input  IN0_2,
  input  IN0_3,
  input  IN0_4,
  input  LOAD0,
  input  IN0_5,
  input  LOAD1,
  input  IN0_6,
  input  IN0_7,
  output OUT0_0,
  output OUT0_1,
  output OUT0_2,
  output OUT0_3,
  output OUT0_4,
  output OUT0_5,
  output OUT0_6,
  output OUT0_7,
  output OUT1_0,
  output OUT1_1,
  output OUT1_2,
  output OUT1_3,
  output OUT1_4,
  output OUT1_5,
  output OUT1_6,
  output OUT1_7
);

  wire controlled_buffer_1_out, controlled_buffer_2_out, controlled_buffer_3_out, controlled_buffer_4_out,
       controlled_buffer_5_out, controlled_buffer_6_out, controlled_buffer_7_out, controlled_buffer_8_out,
       d_ff_1_out_10, d_ff_1_out_11, d_ff_1_out_12, d_ff_1_out_13, d_ff_1_out_14, d_ff_1_out_15,
       d_ff_1_out_16, d_ff_1_out_17, not_1_out, not_2_out;

  assign controlled_buffer_1_out = SET ? IN0_0 : 1'bz;  // Controlled_Buffer controlled_buffer_1
  assign controlled_buffer_2_out = SET ? IN0_1 : 1'bz;  // Controlled_Buffer controlled_buffer_2
  assign controlled_buffer_3_out = SET ? IN0_2 : 1'bz;  // Controlled_Buffer controlled_buffer_3
  assign controlled_buffer_4_out = SET ? IN0_3 : 1'bz;  // Controlled_Buffer controlled_buffer_4
  assign controlled_buffer_5_out = SET ? IN0_4 : 1'bz;  // Controlled_Buffer controlled_buffer_5
  assign controlled_buffer_6_out = SET ? IN0_5 : 1'bz;  // Controlled_Buffer controlled_buffer_6
  assign controlled_buffer_7_out = SET ? IN0_6 : 1'bz;  // Controlled_Buffer controlled_buffer_7
  assign controlled_buffer_8_out = SET ? IN0_7 : 1'bz;  // Controlled_Buffer controlled_buffer_8
  not not_1 (not_1_out, SET);
  not not_2 (not_2_out, not_1_out);
  D_FF d_ff_1 (
    .Clock(not_2_out), .D0(controlled_buffer_1_out), .D1(controlled_buffer_2_out),
    .D2(controlled_buffer_3_out), .D3(controlled_buffer_4_out), .D4(controlled_buffer_5_out),
    .D5(controlled_buffer_6_out), .D6(controlled_buffer_7_out), .D7(controlled_buffer_8_out),
    .out_10(d_ff_1_out_10), .out_11(d_ff_1_out_11), .out_12(d_ff_1_out_12), .out_13(d_ff_1_out_13),
    .out_14(d_ff_1_out_14), .out_15(d_ff_1_out_15), .out_16(d_ff_1_out_16), .out_17(d_ff_1_out_17));
  assign OUT0_0 = LOAD0 ? d_ff_1_out_10 : 1'bz;  // Controlled_Buffer controlled_buffer_9
  assign OUT0_1 = LOAD0 ? d_ff_1_out_11 : 1'bz;  // Controlled_Buffer controlled_buffer_10
  assign OUT0_2 = LOAD0 ? d_ff_1_out_12 : 1'bz;  // Controlled_Buffer controlled_buffer_11
  assign OUT0_3 = LOAD0 ? d_ff_1_out_13 : 1'bz;  // Controlled_Buffer controlled_buffer_12
  assign OUT0_4 = LOAD0 ? d_ff_1_out_14 : 1'bz;  // Controlled_Buffer controlled_buffer_13
  assign OUT0_5 = LOAD0 ? d_ff_1_out_15 : 1'bz;  // Controlled_Buffer controlled_buffer_14
  assign OUT0_6 = LOAD0 ? d_ff_1_out_16 : 1'bz;  // Controlled_Buffer controlled_buffer_15
  assign OUT0_7 = LOAD0 ? d_ff_1_out_17 : 1'bz;  // Controlled_Buffer controlled_buffer_16
  assign OUT1_0 = LOAD1 ? d_ff_1_out_10 : 1'bz;  // Controlled_Buffer controlled_buffer_17
  assign OUT1_1 = LOAD1 ? d_ff_1_out_11 : 1'bz;  // Controlled_Buffer controlled_buffer_18
  assign OUT1_2 = LOAD1 ? d_ff_1_out_12 : 1'bz;  // Controlled_Buffer controlled_buffer_19
  assign OUT1_3 = LOAD1 ? d_ff_1_out_13 : 1'bz;  // Controlled_Buffer controlled_buffer_20
  assign OUT1_4 = LOAD1 ? d_ff_1_out_14 : 1'bz;  // Controlled_Buffer controlled_buffer_21
  assign OUT1_5 = LOAD1 ? d_ff_1_out_15 : 1'bz;  // Controlled_Buffer controlled_buffer_22
  assign OUT1_6 = LOAD1 ? d_ff_1_out_16 : 1'bz;  // Controlled_Buffer controlled_buffer_23
  assign OUT1_7 = LOAD1 ? d_ff_1_out_17 : 1'bz;  // Controlled_Buffer controlled_buffer_24
endmodule

module _16bit_Register (
  input  SET_L,
  input  SET_H,
  input  [7:0] IN_L,
  input  LOAD_L,
  input  LOAD_16,
  input  LOAD_H,
  input  [7:0] IN_H,
  output [7:0] OUT_L,
  output [7:0] OUT_H,
  output [15:0] _16OUT
);

  Register register_1 (
    .IN0_0(IN_L[0]), .IN0_1(IN_L[1]), .IN0_2(IN_L[2]), .IN0_3(IN_L[3]), .IN0_4(IN_L[4]), .IN0_5(IN_L[5]),
    .IN0_6(IN_L[6]), .IN0_7(IN_L[7]), .SET(SET_L), .LOAD0(LOAD_L), .LOAD1(LOAD_16), .OUT0_0(OUT_L[0]),
    .OUT0_1(OUT_L[1]), .OUT0_2(OUT_L[2]), .OUT0_3(OUT_L[3]), .OUT0_4(OUT_L[4]), .OUT0_5(OUT_L[5]),
    .OUT0_6(OUT_L[6]), .OUT0_7(OUT_L[7]), .OUT1_0(_16OUT[0]), .OUT1_1(_16OUT[1]), .OUT1_2(_16OUT[2]),
    .OUT1_3(_16OUT[3]), .OUT1_4(_16OUT[4]), .OUT1_5(_16OUT[5]), .OUT1_6(_16OUT[6]), .OUT1_7(_16OUT[7]));
  Register register_2 (
    .IN0_0(IN_H[0]), .IN0_1(IN_H[1]), .IN0_2(IN_H[2]), .IN0_3(IN_H[3]), .IN0_4(IN_H[4]), .IN0_5(IN_H[5]),
    .IN0_6(IN_H[6]), .IN0_7(IN_H[7]), .SET(SET_H), .LOAD0(LOAD_H), .LOAD1(LOAD_16), .OUT0_0(OUT_H[0]),
    .OUT0_1(OUT_H[1]), .OUT0_2(OUT_H[2]), .OUT0_3(OUT_H[3]), .OUT0_4(OUT_H[4]), .OUT0_5(OUT_H[5]),
    .OUT0_6(OUT_H[6]), .OUT0_7(OUT_H[7]), .OUT1_0(_16OUT[8]), .OUT1_1(_16OUT[9]), .OUT1_2(_16OUT[10]),
    .OUT1_3(_16OUT[11]), .OUT1_4(_16OUT[12]), .OUT1_5(_16OUT[13]), .OUT1_6(_16OUT[14]), .OUT1_7(_16OUT[15]));
endmodule

module Zero_detect (
  input  BUS0,
  input  BUS1,
  input  BUS2,
  input  BUS3,
  input  BUS4,
  input  BUS5,
  input  BUS6,
  input  BUS7,
  output ZERO
);

  wire and_1_out, and_2_out, and_3_out, and_4_out, and_5_out, and_7_out, not_1_out, not_2_out, not_3_out,
       not_4_out, not_5_out, not_6_out, not_7_out, not_8_out;

  Pull_Resistor pull_resistor_1 (.node(BUS0));
  Pull_Resistor pull_resistor_2 (.node(BUS2));
  Pull_Resistor pull_resistor_3 (.node(BUS1));
  Pull_Resistor pull_resistor_4 (.node(BUS3));
  Pull_Resistor pull_resistor_5 (.node(BUS6));
  Pull_Resistor pull_resistor_6 (.node(BUS5));
  Pull_Resistor pull_resistor_7 (.node(BUS4));
  Pull_Resistor pull_resistor_8 (.node(BUS7));
  not not_1 (not_1_out, BUS0);
  not not_2 (not_2_out, BUS1);
  not not_3 (not_3_out, BUS2);
  not not_4 (not_4_out, BUS3);
  not not_5 (not_5_out, BUS4);
  not not_6 (not_6_out, BUS5);
  not not_7 (not_7_out, BUS6);
  not not_8 (not_8_out, BUS7);
  and and_1 (and_1_out, not_1_out, not_2_out);
  and and_2 (and_2_out, not_3_out, not_4_out);
  and and_3 (and_3_out, not_5_out, not_6_out);
  and and_4 (and_4_out, not_7_out, not_8_out);
  and and_5 (and_5_out, and_1_out, and_2_out);
  and and_6 (ZERO, and_5_out, and_7_out);
  and and_7 (and_7_out, and_3_out, and_4_out);
endmodule
